# Fritzing sketch arduino_BlinkM (saved by Fritzing 0.8.0b)
breadboards: 1

parts:
  LED1 = RGB LED (com. cathode, rgb) [package="5 mm [THT]"]
  R1 = Resistor [tolerance=±5% resistance=330 package="0603 [SMD]"]
  R3 = Resistor [tolerance=±5% resistance=330 package="0603 [SMD]"]
  R4 = Resistor [tolerance=±5% resistance=330 package="0603 [SMD]"]
  U1 = attiny85 [package=dip]
  Composants1 = Arduino Micro (Rev3)  # not connected

nets:
  N1: LED1.red_anode, R3.Pin_0
  N2: LED1.common_cathode, U1.Pin_4
  N3: LED1.green_anode, R4.Pin_0
  N4: LED1.blue_anode, R1.Pin_0
  N5: R1.Pin_1, U1.Pin_3
  N6: R3.Pin_1, U1.Pin_6
  N7: R4.Pin_1, U1.Pin_2
