# Fritzing sketch tag2rgb (saved by Fritzing 0.7.12b)
breadboards: 1

parts:
  Arduino1 = Arduino
  LED1 = RGB LED (com. cathode, rbg) [package="5 mm [THT]"]
  R1 = Resistor [tolerance=±5% resistance=330 package=THT]
  R2 = Resistor [tolerance=±5% resistance=330 package=THT]
  R3 = Resistor [tolerance=±5% resistance=330 package=THT]

nets:
  N1: Arduino1.D6, R2.Pin_1
  N2: Arduino1.D5, R3.Pin_1
  N3: Arduino1.D3, R1.Pin_1
  N4: Arduino1.+5V, LED1.blue_anode
  N5: LED1.red_anode, R2.Pin_0
  N6: LED1.common_cathode, R3.Pin_0
  N7: LED1.green_anode, R1.Pin_0

notes:
  SPI shield NFC
